# Fritzing sketch board_setup (saved by Fritzing 1.0.5)
breadboards: 1

parts:
  RP1 = WaveShare RP2350 LCD-1.28 Connector
  R1 = Isolated5 Resistor-5 (SIP-10) [tolerance=±5% resistance=100 package=SIP-10]
  LED2 = RGB LED (com. anode, rbg) [color="Red (633nm)" current=0.030A package="5 mm [THT]"]
  Part1 = Thumb Joystick
  LED3 = LED - 5mm [color="Red (633nm)" current=0.030A package="5 mm [THT]"]
  U1 = LM-324N quadruple operational Amplifier [part_number=LM324N package="DIP (Dual Inline) [THT]"]
  Part2 = LM-324N quadruple operational Amplifier [part_number=LM324N package="DIP (Dual Inline) [THT]"]  # not connected
  U1_1 = LM-324N quadruple operational Amplifier [part_number=LM324N package="DIP (Dual Inline) [THT]"]  # not connected
  U1_2 = LM-324N quadruple operational Amplifier [part_number=LM324N package="DIP (Dual Inline) [THT]"]  # not connected
  U1_3 = LM-324N quadruple operational Amplifier [part_number=LM324N package="DIP (Dual Inline) [THT]"]  # not connected
  U1_4 = LM-324N quadruple operational Amplifier [part_number=LM324N package="DIP (Dual Inline) [THT]"]  # not connected
  R2 = Resistor [tolerance=±5% power=0.25W resistance=10k package=THT]
  R3 = Resistor [tolerance=±5% power=0.25W resistance=10k package=THT]
  DCF1 = KundoXT DCF77 antenna

nets:
  N1: RP1.5, R1.Pin_4
  N2: RP1.4, R1.Pin_2
  N3: RP1.3, R1.Pin_0
  N4: RP1.1, R1.Pin_6
  N5: RP1.13, U1.connector0, R3.Pin_0
  N6: RP1.20, Part1.HORZ
  N7: RP1.ADC, Part1.SEL, U1.connector3, DCF1.UB+
  N8: RP1.27, Part1.VCC
  N9: RP1.26, Part1.VERT
  GND: RP1.GND, LED2.common_anode, Part1.GND, LED3.anode, U1.connector10, R3.Pin_1, DCF1.Enable, DCF1.GND
  N10: R1.Pin_1, LED2.green_cathode
  N11: R1.Pin_3, LED2.blue_cathode
  N12: R1.Pin_5, LED2.red_cathode
  N13: R1.Pin_7, LED3.cathode
  N14: U1.connector1, R2.Pin_0
  N15: U1.connector2, R2.Pin_1, DCF1.Signal

custom parts:
  WaveShare RP2350 LCD-1.28 Connector: WaveShare RP2350 LCD-1.28 on a PCB designed at the HS-Esslingen
  Isolated5 Resistor-5 (SIP-10): A resistor array is a single package which contains more than one resistor. They are typically used for convenience when several resistors are needed together in the same place in a circuit.
  LM-324N quadruple operational Amplifier: LM-324N Quadruple Op-Amp
  LM-324N quadruple operational Amplifier: LM-324N Quadruple Op-Amp
  LM-324N quadruple operational Amplifier: LM-324N Quadruple Op-Amp
  LM-324N quadruple operational Amplifier: LM-324N Quadruple Op-Amp
  LM-324N quadruple operational Amplifier: LM-324N Quadruple Op-Amp
  LM-324N quadruple operational Amplifier: LM-324N Quadruple Op-Amp
  KundoXT DCF77 antenna: KundoXT DCF77 antenna and PCB available from Reichelt
